# Fritzing sketch montaje_proyecto_en_breadboard_v7 (saved by Fritzing 0.9.10b)
breadboards: 2

parts:
  WeMos_D1_Mini1 = WeMos D1 Mini
  Q1 = TRANSISTOR_NPN [package=to-92-ammo]
  S1 = Momentary Switch [package=ksa_sealed_tac_switch]
  S2 = Momentary Switch [package=ksa_sealed_tac_switch]
  S3 = Momentary Switch [package=ksa_sealed_tac_switch]
  S4 = Momentary Switch [package=ksa_sealed_tac_switch]
  IC1 = DS1307 [package=THT]
  XTAL3 = CRYSTAL - kHz [frequency="32 kHz"]
  Componente1 = TRRS 3.5mm Jack Breakout
  R9 = Resistor [tolerance=±10% power=0.5W resistance=220 package=THT]
  R12 = Resistor [tolerance=±10% power=0.5W resistance=2200 package=THT]
  R14 = Resistor [tolerance=±10% power=0.5W resistance=5100 package=THT]
  R15 = Resistor [tolerance=±10% power=0.5W resistance=10000 package=THT]
  R16 = Resistor [tolerance=±10% power=0.5W resistance=10000 package=THT]
  J3 = Generic female header - 6 pins [form="♀ (female)" package=THT]
  R17 = Resistor [tolerance=±10% power=0.5W resistance=10000 package=THT]
  R18 = Resistor [tolerance=±10% power=0.5W resistance=10000 package=THT]
  J5 = shrouded pin header, 12 pins [form="♂ (shrouded male)"]
  R20 = Resistor [tolerance=±10% power=0.5W resistance=10000 package=THT]
  R21 = Resistor [tolerance=±10% power=0.5W resistance=10000 package=THT]
  J7 = Generic female header - 4 pins [form="♀ (female)" package=THT]
  J10 = Generic male header - 4 pins [form="♂ (male)" package=THT]
  J11 = Generic male header - 3 pins [form="♂ (male)" package=THT]
  J6 = Generic female header - 6 pins [form="♀ (female)" package=THT]
  J13 = Generic male header - 3 pins [form="♂ (male)" package=THT]
  R22 = Resistor [tolerance=±10% power=0.5W resistance=10000 package=THT]
  R23 = Resistor [tolerance=±10% power=0.5W resistance=10000 package=THT]

nets:
  VCC: WeMos_D1_Mini1.3V3, Q1.C, S1.3, S2.3, S3.3, S4.3, IC1.+V, R9.Pin_0, R12.Pin_0, R14.Pin_0, R16.Pin_0, J3.VCC, R20.Pin_0, R21.Pin_0, J7.VCC, J10.VCC
  N1: WeMos_D1_Mini1.A0, R18.Pin_1, J5.pin4, J5.pin9
  N2: WeMos_D1_Mini1.D0, S1.1
  N3: WeMos_D1_Mini1.D1, IC1.SCL_-_I2C_Clock, J3.SCL, R20.Pin_1, J7.SCL, J10.SCL
  N4: WeMos_D1_Mini1.D2, IC1.SDA_-_I2C_Data, J3.SDA, R21.Pin_1, J7.SDA, J10.SDA
  N5: WeMos_D1_Mini1.D5, S2.1
  N6: WeMos_D1_Mini1.D6, S3.1
  N7: WeMos_D1_Mini1.D7, S4.1
  GND: WeMos_D1_Mini1.G, IC1.0V, Componente1.TIP, R15.Pin_0, J3.GND, R17.Pin_0, R18.Pin_0, J7.GND, J10.GND, J11.GND, J6.OUT-#0, J13.GND, R22.Pin_0, R23.Pin_0
  N8: Q1.E, J13.Vout
  N9: Q1.B, J11.I/O
  N10: S1.2, R17.Pin_1
  N11: S2.2, R15.Pin_1
  N12: S3.2, R22.Pin_1
  N13: S4.2, R23.Pin_1
  N14: IC1.X1_-_Crystal, XTAL3.pin_1
  N15: IC1.X2_-_Crystal, XTAL3.pin_0
  N16: Componente1.SLEEVE, J3.VIN+
  N17: Componente1.RING2, J3.VIN-
  N18: R9.Pin_1, J5.pin1, J5.pin12
  N19: R12.Pin_1, J5.pin2, J5.pin11
  N20: R14.Pin_1, J5.pin5, J5.pin8
  N21: R16.Pin_1, J5.pin6, J5.pin7
  N22: J5.pin3, J5.pin10
  VCC_2: J11.VCC, J6.OUT-#3, J13.VCC

notes:
  Color cables:
  Voltaje:
  Rojo -> 3.3 V
  Negro -> GND (0V)
  I2C:
  Amarillo ->SDA
  Verde -> SCL / SCK
  Medidor INA219 (< 26V <3.2A):
  Marrón -> VIN +
  Rosa -> VIN -
  Botones 1, 2, 3, y 4:
  Naranja -> D0, D5, D6, y D7
  Divisor resistivo interruptor deslizante:
  Ocre -> A0
  Generador de pulsos:
  Cian -> D4
  Morado -> No usar estos pines
  Resistencias (11 uds):
  DS1307:
  2 x 10K Ohm
  Botones:
  4 x 10K Ohm
  Divisor resistivo interruptor deslizante:
  1x 220 Ohm
  1x 2K Ohm
  1 x 5.1K Ohm
  2 x 10K Ohm
  Regulador tensión a 3.3V:
  AMS1117-3.3
  Transistor NPN:
  BC547 (CBE) TO-92
  Cristal cuarzo:
  32.768 KHz
  Entrada de voltaje de la batería:
  3.2V a 4.2V
  Batería 3.7V
  Dirección I2C:
  0x3C -> OLED SSD1306
  0x40 -> HTU21D
  0x45 -> INA219
  0x68 -> DS1307

custom parts:
  Generic female header - 6 pins: Generic female header
  Generic female header - 4 pins: Generic female header
  Generic male header - 4 pins: Generic male header
  Generic male header - 3 pins: Generic male header
  Generic female header - 6 pins: Generic female header
  Generic male header - 3 pins: Generic male header
